# Fritzing sketch Clock Display (saved by Fritzing 0.9.3b)
breadboards: 2

parts:
  U1 = 74HC595 [package="DIP16 [THT]"]
  R1 = Resistor [tolerance=±5% resistance=270 package="0402 [SMD]"]
  R2 = Resistor [tolerance=±5% resistance=270 package="0402 [SMD]"]
  R3 = Resistor [tolerance=±5% resistance=270 package="0402 [SMD]"]
  R4 = Resistor [tolerance=±5% resistance=270 package="0402 [SMD]"]
  R5 = Resistor [tolerance=±5% resistance=270 package="0402 [SMD]"]
  R6 = Resistor [tolerance=±5% resistance=270 package="0402 [SMD]"]
  R7 = Resistor [tolerance=±5% resistance=270 package="0402 [SMD]"]
  R8 = Resistor [tolerance=±5% resistance=220 package="0402 [SMD]"]
  LED3 = 7-SEGMENT-4DIGIT-ATA8041AB [part_number=ATA8041AB package=7-segment-4digit-youngsun-longpads]
  Part1 = Arduino Pro Mini (5V)

nets:
  N1: U1.Q1, R7.Pin_1
  N2: U1.Q2, R4.Pin_1
  N3: U1.Q3, R5.Pin_1
  N4: U1.Q4, R3.Pin_1
  N5: U1.Q5, R2.Pin_1
  N6: U1.Q6, R1.Pin_1
  N7: U1.Q7, R8.Pin_1
  N8: U1.GND, U1.OE
  VCC: U1.MR, U1.VCC, Part1.VCC
  N9: U1.Q0, R6.Pin_1
  N10: R1.Pin_0, LED3.10
  N11: R2.Pin_0, LED3.5
  N12: R3.Pin_0, LED3.4
  N13: R4.Pin_0, LED3.2
  N14: R5.Pin_0, LED3.3
  N15: R6.Pin_0, LED3.11
  N16: R7.Pin_0, LED3.1
  N17: R8.Pin_0, LED3.7
